# Fritzing sketch TrafficLight Mini Auto V9 Ethernet Make2 (saved by Fritzing 0.9.2b)
breadboards: 1

parts:
  ArduinoUNO = Arduino Uno (Rev3)
  D8 = Rectifier Diode [part_number=1N4001 package="300 mil [THT]"]
  D9 = Rectifier Diode [part_number=1N4001 package="300 mil [THT]"]
  D10 = Rectifier Diode [part_number=1N4001 package="300 mil [THT]"]
  D11 = Rectifier Diode [part_number=1N4001 package="300 mil [THT]"]
  D12 = Rectifier Diode [part_number=1N4001 package="300 mil [THT]"]
  D13 = Rectifier Diode [part_number=1N4001 package="300 mil [THT]"]
  D14 = Rectifier Diode [part_number=1N4001 package="300 mil [THT]"]
  LED25 = LED - 5mm [color="Red (633nm)" package="5 mm [THT]"]
  LED27 = LED - 5mm [color="Red (633nm)" package="5 mm [THT]"]
  LED28 = LED - 5mm [color="Red (633nm)" package="5 mm [THT]"]
  LED29 = LED - 5mm [color="Red (633nm)" package="5 mm [THT]"]
  LED35 = LED - 5mm [color="Red (633nm)" package="5 mm [THT]"]
  LED41 = LED - 5mm [color="Yellow (585nm)" package="5 mm [THT]"]
  LED43 = LED - 5mm [color="Green (555nm)" package="5 mm [THT]"]
  LED47 = LED - 5mm [color="Yellow (585nm)" package="5 mm [THT]"]
  LED48 = LED - 5mm [color="Yellow (585nm)" package="5 mm [THT]"]
  LED49 = LED - 5mm [color="Red (633nm)" package="5 mm [THT]"]
  LED50 = LED - 5mm [color="Red (633nm)" package="5 mm [THT]"]
  LED51 = LED - 5mm [color="Red (633nm)" package="5 mm [THT]"]
  LED53 = LED - 5mm [color="Yellow (585nm)" package="5 mm [THT]"]
  LED54 = LED - 5mm [color="Green (555nm)" package="5 mm [THT]"]
  LED55 = LED - 5mm [color="Green (555nm)" package="5 mm [THT]"]
  LED56 = LED - 5mm [color="Green (555nm)" package="5 mm [THT]"]
  LED57 = LED - 5mm [color="Green (555nm)" package="5 mm [THT]"]
  LED58 = LED - 5mm [color="Green (555nm)" package="5 mm [THT]"]
  LED59 = LED - 5mm [color="Green (555nm)" package="5 mm [THT]"]
  LED61 = LED - 5mm [color="Yellow (585nm)" package="5 mm [THT]"]
  LED67 = LED - 5mm [color="Green (555nm)" package="5 mm [THT]"]
  LED68 = LED - 5mm [color="Yellow (585nm)" package="5 mm [THT]"]
  LED69 = LED - 5mm [color="Yellow (585nm)" package="5 mm [THT]"]
  LED70 = LED - 5mm [color="Yellow (585nm)" package="5 mm [THT]"]
  S1 = Pushbutton [package="[THT]"]
  R1 = Resistor [tolerance=±5% resistance=10k package=THT]
  ArduinoEthernetShield = Arduino Ethernet Shield (Rev3)

nets:
  N1: ArduinoUNO.GND, D8.cathode
  N2: D8.anode, D9.cathode, D10.cathode, D11.cathode, D12.cathode, D13.cathode, D14.cathode, R1.Pin_1
  N3: D9.anode, LED61.anode, LED68.anode, LED69.anode, LED70.anode
  N4: D10.anode, LED27.anode, LED29.anode, LED49.anode, LED50.anode
  N5: D11.anode, LED41.anode, LED47.anode, LED48.anode, LED53.anode
  N6: D12.anode, LED25.anode, LED28.anode, LED35.anode, LED51.anode
  N7: D13.anode, LED56.anode, LED57.anode, LED58.anode, LED59.anode
  N8: D14.anode, LED43.anode, LED54.anode, LED55.anode, LED67.anode
  N9: LED25.cathode, LED27.cathode, LED28.cathode, LED29.cathode, LED35.cathode, LED49.cathode, LED50.cathode, LED51.cathode, ArduinoEthernetShield.PWM_D3
  N10: LED41.cathode, LED47.cathode, LED48.cathode, LED53.cathode, LED61.cathode, LED68.cathode, LED69.cathode, LED70.cathode, ArduinoEthernetShield.PWM_D5
  N11: LED43.cathode, LED54.cathode, LED55.cathode, LED56.cathode, LED57.cathode, LED58.cathode, LED59.cathode, LED67.cathode, ArduinoEthernetShield.PWM_D6
  N12: S1.Pin_1, S1.Pin_2, ArduinoEthernetShield.5V
  N13: S1.Pin_3, S1.Pin_4, R1.Pin_0, ArduinoEthernetShield.D2

notes:
  To go into Emergency Mode: Hold the Emergency Button and press RESET
  <-Emergency
  Ethernet Shield Edition
  Image with Arduino UNO

// code stored in the sketch: TrafficLight_Mini_Auto_V8.ino
void setup() {
  //sets up pins 2,3,4 as outputs
  pinMode(2, OUTPUT);
  pinMode(3, OUTPUT);
  pinMode(4, OUTPUT);
}

void loop() {
  // do RED for 10sec, green for 10sec, and yellow for 3sec.
digitalWrite(2 , HIGH);
delay(10000);
digitalWrite(2 ,LOW);
digitalWrite(4 ,HIGH);
delay(10000);
digitalWrite(4 ,LOW);
digitalWrite(3 ,HIGH);
delay(3000);
digitalWrite(3 , LOW);
}
/* Notes:
Press the RESET button on your board to restart the circuit, putting it back on RED.
*/

// code stored in the sketch: TrafficLight_Mini_Auto_V9.ino
int emergency = 0;
void setup() {
  //sets up pins 3,4,5 as outputs
  pinMode(3, OUTPUT);
  pinMode(4, OUTPUT);
  pinMode(5, OUTPUT);
  pinMode(13, OUTPUT); //set up pin13LED as output
  pinMode(2, INPUT); //set up emergency switch as input
}

void loop() {
  emergency = digitalRead(2);
  if (emergency == LOW) {
   // do RED for 10sec, green for 10sec, and yellow for 3sec.
digitalWrite(13, LOW);
digitalWrite(3 , HIGH);
delay(10000);
digitalWrite(13, HIGH);
digitalWrite(3 ,LOW);
digitalWrite(5 ,HIGH);
delay(10000);
digitalWrite(5 ,LOW);
digitalWrite(4 ,HIGH);
delay(3000);
digitalWrite(4 , LOW);
  }
    else{
   digitalWrite(3, HIGH);
    digitalWrite(13, LOW);
    delay(1000);
    digitalWrite(3, LOW);
    digitalWrite(13, HIGH);
    delay(1000);
}
}
/* Notes:
Press the RESET button on your board to restart the circuit, putting it back on RED.
To go into Emergency Mode: Hold the Emergency Button and press RESET.
*/

// code stored in the sketch: TrafficLight_Mini_Auto_V9_Ethernet.ino
//This Sketch has been modified for users of the Ethernet Shield.
int emergency = 0;
void setup() {
  //sets up pins 3,4,5 as outputs
  pinMode(3, OUTPUT);
  pinMode(5, OUTPUT);
  pinMode(6, OUTPUT);
  pinMode(2, INPUT); //set up emergency switch as input
}

void loop() {
  emergency = digitalRead(2);
  if (emergency == LOW) {
   // do RED for 10sec, green for 10sec, and yellow for 3sec.
digitalWrite(3 , HIGH);
delay(10000);
digitalWrite(3 ,LOW);
digitalWrite(6 ,HIGH);
delay(10000);
digitalWrite(6 ,LOW);
digitalWrite(5 ,HIGH);
delay(3000);
digitalWrite(5 , LOW);
  }
    else{
   digitalWrite(3, HIGH);
    delay(1000);
    digitalWrite(3, LOW);
    delay(1000);
}}
/* Notes:
Press the RESET button on your board to restart the circuit, putting it back on RED.
To go into Emergency Mode: Hold the Emergency Button and press RESET.
*/
